# Fritzing sketch Riego (saved by Fritzing 0.9.3b)

parts:
  Componente1 = Arduino Sensor Shield v5.0
  Componente2 = FC-28 Soil Hygrometer Module
  YL-83_-_Control_Board1 = YL-83 Rain Sensor - Control Board
  Componente3 = FC-28 Soil Hygrometer Module - Probe
  Componente4 = LCD1602-I2C
  U1 = POT [package=pot_mammoth]
  U2 = 4-Channel 5v Relay Shield [package=relay-4ch5v10a]
  M1 = DC Motor
  BATT1 = 4xAA Switchable Battery Pack w/Bare Wire
  YL-83_-_Detection_Board1 = YL-83 Rain Sensor - Detection Board

nets:
  N1: Componente1.A1, Componente2.AO
  N2: Componente1.A2, YL-83_-_Control_Board1.AO
  N3: Componente1.A3, U1.A
  N4: Componente1.GND#38, Componente4.GND
  N5: Componente1.+5V#65, Componente1.SCL, Componente4.VCC, Componente4.SCL
  GND: Componente1.D11, Componente1.GND#133, Componente1.GND#134, Componente1.GND#135, Componente2.GND, YL-83_-_Control_Board1.GND, U1.S
  N6: Componente1.D13, U2.IN4
  N7: Componente1.GND#72, Componente1.GND#118, U2.GND
  N8: Componente1.SDA, Componente4.SDA
  N9: Componente1.+5V#94, Componente1.+5V#103, U2.VCC
  N10: Componente1.+5V#139, Componente2.VCC
  N11: Componente1.+5V#140, YL-83_-_Control_Board1.VCC
  N12: Componente1.+5V#141, U1.E
  N13: Componente2.POS, Componente3.POS
  N14: Componente2.NEG, Componente3.NEG
  N15: YL-83_-_Control_Board1.POS, YL-83_-_Detection_Board1.POS
  N16: YL-83_-_Control_Board1.NEG, YL-83_-_Detection_Board1.NEG
  N17: U2.K4-On, M1.pin_2
  N18: M1.pin_1, BATT1.NEG

custom parts:
  FC-28 Soil Hygrometer Module: The FC-28 is a soil hygrometer module that uses the Texas Instruments LM393 comparator chip to provide an analog measurement of soil humidity. The digital output is high when soil moisture is over a certain threshold, as determined by adjusting the potentiometer.
  YL-83 Rain Sensor - Control Board: The YL-83 is a rain sensor that has more resistance when dry and less resistance when wet. The module runs at 5V.
  FC-28 Soil Hygrometer Module - Probe: The FC-28 is a soil hygrometer module that uses the Texas Instruments LM393 comparator chip to provide an analog measurement of soil humidity.
  LCD1602-I2C: A standard character display, usually with 2x16 characters. Comes in many colors with LCM1602 IIC attached.
  4-Channel 5v Relay Shield: 4 Channel 5v Relay Shield w. 2x SPD-06VDC-SD-C
  4xAA Switchable Battery Pack w/Bare Wire: 4xAA Switchable Battery Pack with Bare Wire connection
  YL-83 Rain Sensor - Detection Board: The YL-83 is a rain sensor that has more resistance when dry and less resistance when wet. The module runs at 5V.
